// Logisim project SmartWaterTankControlSystem.circ as structural Verilog: 1 circuit, main circuit main
module main (
  input  SO,
  input  S1,
  input  S2,
  input  S3,
  input  in_5,
  input  PUMP,
  output C0,
  output C1,
  output ALARM,
  output out_10,
  output LOW,
  output out_12,
  output MEDIUM,
  output FULL
);

  wire and_2_out, and_3_out, and_5_out, and_6_out, clock_1_out, L0_out, L1_out, not_3_out, not_4_out,
       or_1_out, or_2_out;
  wire [3:0] bit_extender_1_out;

  D_Flip_Flop FF0 (.clk(clock_1_out), .D(L0_out), .Q(out_12));  // open: Qn, preset, en, reset
  Clock clock_1 (.out(clock_1_out));
  assign bit_extender_1_out = {{2{1'b0}}, {out_10, out_12}};  // Bit_Extender bit_extender_1
  or L0 (L0_out, S1, S3);
  // Probe on L0_out
  // Probe on L1_out
  or L1 (L1_out, S2, S3);
  D_Flip_Flop FF1 (.clk(clock_1_out), .D(L1_out), .Q(out_10));  // open: Qn, preset, en, reset
  Hex_Digit_Display hex_digit_display_1 (.value(bit_extender_1_out));  // open: dp
  and and_1 (FULL, out_10, out_12);
  and and_2 (and_2_out, L0_out, L1_out);
  not not_1 (LOW, out_10);
  not not_2 (MEDIUM, out_12);
  not not_3 (not_3_out, and_2_out);
  // Probe on not_3_out
  Counter #(.width(2), .max('h3)) counter_1 (.clk(clock_1_out));  // open: load, D, count, Q, carry, clr
  nand nand_1 (PUMP, out_10, out_12);
  and and_3 (and_3_out, MEDIUM, LOW);
  D_Flip_Flop COUNTER_FF0 (.clk(clock_1_out), .D(and_5_out), .Q(C0));  // open: Qn, preset, en, reset
  not not_4 (not_4_out, C0);
  D_Flip_Flop COUNTER_FF1 (.clk(clock_1_out), .D(and_6_out), .Q(C1));  // open: Qn, preset, en, reset
  and and_4 (ALARM, C1, C0);
  or or_1 (or_1_out, C1, not_4_out);
  or or_2 (or_2_out, C0, C1);
  and and_5 (and_5_out, FULL, or_1_out);
  and and_6 (and_6_out, FULL, or_2_out);
endmodule
